# Fritzing sketch Tito (saved by Fritzing 0.9.6b)
breadboards: 1

parts:
  Componente1 = Arduino Uno (Rev3)
  IR1 = TSOP312.., 314.. [package=THT]
  IC1 = L293D [package=THT]
  LED1 = RGB LED - (4 legs) [package="5 mm [THT]"]
  M1 = gear-motor
  M2 = gear-motor
  R1 = Resistor [tolerance=±5% power=0.25 resistance=220 package=THT]
  R2 = Resistor [tolerance=±5% power=0.25 resistance=220 package=THT]
  R3 = Resistor [tolerance=±5% power=0.25 resistance=220 package=THT]
  U1 = LIPO-2000mAh [package=lipo-2000]
  S1 = Taiway 100-SP-X-T1 SPDT Miniature Toggle Switch [part_number=100-SP-X-T1-0-0-B1-M1 package=THT]

nets:
  N1: Componente1.D8, R2.Pin_1
  N2: Componente1.D9_PWM, R3.Pin_1
  GND: Componente1.GND, IR1.GND, U1.-
  N3: Componente1.D2, IR1.Data
  N4: Componente1.D3_PWM, IC1.In_2
  N5: Componente1.D4, IC1.In_3
  N6: Componente1.D5_PWM, IC1.In_1
  N7: Componente1.D6_PWM, IC1.In_4
  N8: Componente1.D7, R1.Pin_1
  N9: Componente1.5V, IR1.Vs, LED1.common_anode
  N10: Componente1.VIN, IC1.+Vmotor, S1.L2
  N11: IC1.Enable_1, IC1.Enable_2, IC1.+V
  N12: IC1.Out_1_(_Controlled_by_Enable_1_), M1.pin_1
  N13: IC1.Out_2_(_Controlled_by_Enable_1_), M1.pin_2
  N14: IC1.Out_3_(_Controlled_by_Enable_2_), M2.pin_2
  N15: IC1.Out_4_(_Controlled_by_Enable_2_), M2.pin_1
  N16: LED1.red_cathode, R1.Pin_0
  N17: LED1.green_cathode, R2.Pin_0
  N18: LED1.blue_cathode, R3.Pin_0
  N19: U1.+, S1.COM
